// Logisim project 300230_00.circ as structural Verilog: 1 circuit, main circuit main
module main (
  input  nGPiBSend,
  input  IRQ,
  input  A12,
  input  A13,
  input  A14,
  input  ALE,
  input  nRD,
  input  nWR
);

  wire n74138_1_pin5, n74138_1_pin6, n74138_1_pin11, n74138_1_pin12, n74138_1_pin13, n74138_1_pin14,
       n74138_1_pin15, nand_1_out, not_1_out, not_2_out, not_3_out, not_4_out, or_1_out, or_2_out, or_3_out,
       or_4_out, or_5_out, or_6_out;

  not not_1 (not_1_out, nGPiBSend);
  not not_2 (not_2_out, IRQ);
  nand nand_1 (nand_1_out, nRD, nWR);
  not not_3 (not_3_out, nand_1_out);
  _74138 #(.ShowInternalStructure("true")) u_74138_1 (
    .pin1(A12), .pin2(A13), .pin3(A14), .pin4(ALE), .pin5(n74138_1_pin5), .pin6(n74138_1_pin6),
    .pin15(n74138_1_pin15), .pin14(n74138_1_pin14), .pin13(n74138_1_pin13), .pin12(n74138_1_pin12),
    .pin11(n74138_1_pin11));  // open: pin7, pin10, pin9
  or or_1 (or_1_out, n74138_1_pin11, nWR);
  // Probe on not_1_out
  // Probe on not_2_out
  or or_2 (or_2_out, n74138_1_pin14, not_3_out);
  or or_3 (or_3_out, n74138_1_pin12, nRD);
  // Probe on or_4_out
  or or_4 (or_4_out, nRD, n74138_1_pin11);
  // Probe on not_4_out
  not not_4 (not_4_out, or_1_out);
  or or_5 (or_5_out, n74138_1_pin13, not_3_out);
  or or_6 (or_6_out, or_3_out, not_3_out);
  // Probe on n74138_1_pin15
  // Probe on or_2_out
  // Probe on or_5_out
  // Probe on or_6_out
  // also tied to GND on the sheet: n74138_1_pin5
  // also tied to VCC on the sheet: n74138_1_pin6
endmodule
